# Fritzing sketch esquemaConexiones (saved by Fritzing 0.8.5b)
breadboards: 1

parts:
  Parte1 = Arduino Uno (Rev3)
  R1 = Rotary Potentiometer (Small) [maximum_resistance=100kΩ package=THT]
  LED1 = LED - 5mm [color="Red (633nm)" package="5 mm [THT]"]  # not connected
  R2 = Photocell (LDR) [package=THT]
  LED2 = LED - 5mm [color="Red (633nm)" package="5 mm [THT]"]

nets:
  N1: Parte1.A0, Parte1.5V, R1.wiper, R2.pin_1
  N2: Parte1.D8, LED2.anode
  N3: Parte1.GND, LED2.cathode
  N4: R1.leg2, R2.pin_0
