# Fritzing sketch UNOaMEGA (saved by Fritzing 0.9.2b)

parts:
  Parte1 = Arduino Uno (Rev3)
  Parte3 = Arduino Mega 2560 (Rev3)

nets:
  N1: Parte1.D10_PWM/SS, Parte3.RESET
  N2: Parte1.D11_PWM/MOSI, Parte3.D51
  N3: Parte1.D12/MISO, Parte3.D50
  N4: Parte1.D13/SCK, Parte3.D53
  5V: Parte1.5V, Parte3.5V
  GND: Parte1.GND, Parte3.GND

notes:
  MAESTRO
  ESCLAVO
