# Fritzing sketch UNOaUNO (saved by Fritzing 0.9.2b)

parts:
  Parte1 = Arduino Uno (Rev3)
  Parte2 = Arduino Uno (Rev3)

nets:
  N1: Parte1.D10_PWM/SS, Parte2.RESET
  N2: Parte1.D11_PWM/MOSI, Parte2.D11_PWM/MOSI
  N3: Parte1.D12/MISO, Parte2.D12/MISO
  N4: Parte1.D13/SCK, Parte2.D13/SCK
  5V: Parte1.5V, Parte2.5V
  GND: Parte1.GND, Parte2.GND

notes:
  MAESTRO
  ESCLAVO
