# Fritzing sketch controlOWI535 (saved by Fritzing 0.9.2b)
breadboards: 1

parts:
  Parte1 = Arduino Uno (Rev3)
  IC1 = L293D [package=THT]
  IC2 = L293D [package=THT]
  IC3 = L293D [package=THT]
  VCC1 = Battery
  M1 = DC Motor
  M2 = DC Motor
  M3 = DC Motor
  M4 = DC Motor
  M5 = DC Motor

nets:
  N1: Parte1.D8, IC1.In_4
  N2: Parte1.D9_PWM, IC1.In_3
  N3: Parte1.D10_PWM/SS, IC2.In_1
  N4: Parte1.D11_PWM/MOSI, IC2.In_2
  N5: Parte1.D12/MISO, IC2.In_4
  N6: Parte1.D13/SCK, IC2.In_3
  N7: Parte1.D4, IC3.In_1
  N8: Parte1.D5_PWM, IC3.In_2
  N9: Parte1.D6_PWM, IC1.In_1
  N10: Parte1.D7, IC1.In_2
  N11: Parte1.5V, IC1.Enable_1, IC1.Enable_2, IC1.+V, IC2.Enable_1, IC2.Enable_2, IC2.+V, IC3.Enable_1, IC3.Enable_2, IC3.+V
  N12: Parte1.GND, IC1.0V, IC2.0V, IC2.+Vmotor, IC3.0V, IC3.+Vmotor, VCC1.-
  N13: IC1.Out_1_(_Controlled_by_Enable_1_), M1.pin_2
  N14: IC1.Out_2_(_Controlled_by_Enable_1_), M1.pin_1
  N15: IC1.+Vmotor, VCC1.+
  N16: IC1.Out_3_(_Controlled_by_Enable_2_), M2.pin_2
  N17: IC1.Out_4_(_Controlled_by_Enable_2_), M2.pin_1
  N18: IC2.Out_1_(_Controlled_by_Enable_1_), M3.pin_2
  N19: IC2.Out_2_(_Controlled_by_Enable_1_), M3.pin_1
  N20: IC2.Out_4_(_Controlled_by_Enable_2_), M4.pin_1
  N21: IC3.Out_1_(_Controlled_by_Enable_1_), M5.pin_2
  N22: IC3.Out_2_(_Controlled_by_Enable_1_), M5.pin_1
