# Fritzing sketch montajeElectronico (saved by Fritzing 0.9.2b)
breadboards: 1

parts:
  Arduino1 = Arduino
  LED1 = RGB LED (com. anode, rbg) [package="5 mm [THT]"]

nets:
  N1: Arduino1.D11, LED1.green_cathode
  N2: Arduino1.D9, LED1.red_cathode
