# Fritzing sketch conexionRojosVerdesAzulesyTierras (saved by Fritzing 0.9.2b)
breadboards: 4

parts:
  LED5 = RGB LED (com. cathode, rbg) [package="5 mm [THT]"]
  LED6 = RGB LED (com. cathode, rbg) [package="5 mm [THT]"]
  LED7 = RGB LED (com. cathode, rbg) [package="5 mm [THT]"]
  LED8 = RGB LED (com. cathode, rbg) [package="5 mm [THT]"]
  LED9 = RGB LED (com. cathode, rbg) [package="5 mm [THT]"]  # not connected
  LED10 = RGB LED (com. cathode, rbg) [package="5 mm [THT]"]  # not connected
  LED11 = RGB LED (com. cathode, rbg) [package="5 mm [THT]"]  # not connected
  LED12 = RGB LED (com. cathode, rbg) [package="5 mm [THT]"]
  LED13 = RGB LED (com. cathode, rbg) [package="5 mm [THT]"]
  LED14 = RGB LED (com. cathode, rbg) [package="5 mm [THT]"]  # not connected
  LED15 = RGB LED (com. cathode, rbg) [package="5 mm [THT]"]
  LED16 = RGB LED (com. cathode, rbg) [package="5 mm [THT]"]
  LED17 = RGB LED (com. cathode, rbg) [package="5 mm [THT]"]  # not connected
  LED18 = RGB LED (com. cathode, rbg) [package="5 mm [THT]"]  # not connected
  LED19 = RGB LED (com. cathode, rbg) [package="5 mm [THT]"]  # not connected
  LED20 = RGB LED (com. cathode, rbg) [package="5 mm [THT]"]  # not connected
  LED21 = RGB LED (com. cathode, rbg) [package="5 mm [THT]"]  # not connected
  LED22 = RGB LED (com. cathode, rbg) [package="5 mm [THT]"]  # not connected
  LED23 = RGB LED (com. cathode, rbg) [package="5 mm [THT]"]  # not connected
  LED24 = RGB LED (com. cathode, rbg) [package="5 mm [THT]"]  # not connected
  LED25 = RGB LED (com. cathode, rbg) [package="5 mm [THT]"]  # not connected
  LED26 = RGB LED (com. cathode, rbg) [package="5 mm [THT]"]  # not connected
  LED27 = RGB LED (com. cathode, rbg) [package="5 mm [THT]"]  # not connected
  LED28 = RGB LED (com. cathode, rbg) [package="5 mm [THT]"]  # not connected
  LED29 = RGB LED (com. cathode, rbg) [package="5 mm [THT]"]  # not connected
  LED30 = RGB LED (com. cathode, rbg) [package="5 mm [THT]"]  # not connected
  LED31 = RGB LED (com. cathode, rbg) [package="5 mm [THT]"]  # not connected
  LED32 = RGB LED (com. cathode, rbg) [package="5 mm [THT]"]  # not connected
  R1 = Resistor [tolerance=±5% resistance=220 package=THT]
  R2 = Resistor [tolerance=±5% resistance=220 package=THT]
  R3 = Resistor [tolerance=±5% resistance=220 package=THT]  # not connected
  R4 = Resistor [tolerance=±5% resistance=220 package=THT]  # not connected
  R5 = Resistor [tolerance=±5% resistance=220 package=THT]  # not connected
  R6 = Resistor [tolerance=±5% resistance=220 package=THT]  # not connected
  R7 = Resistor [tolerance=±5% resistance=220 package=THT]  # not connected
  R8 = Resistor [tolerance=±5% resistance=220 package=THT]  # not connected
  R9 = Resistor [tolerance=±5% resistance=220 package=THT]
  R10 = Resistor [tolerance=±5% resistance=220 package=THT]
  R11 = Resistor [tolerance=±5% resistance=220 package=THT]  # not connected
  R12 = Resistor [tolerance=±5% resistance=220 package=THT]  # not connected
  R13 = Resistor [tolerance=±5% resistance=220 package=THT]  # not connected
  R14 = Resistor [tolerance=±5% resistance=220 package=THT]  # not connected
  R15 = Resistor [tolerance=±5% resistance=220 package=THT]  # not connected
  R16 = Resistor [tolerance=±5% resistance=220 package=THT]  # not connected
  R17 = Resistor [tolerance=±5% resistance=220 package=THT]
  R18 = Resistor [tolerance=±5% resistance=220 package=THT]
  R19 = Resistor [tolerance=±5% resistance=220 package=THT]  # not connected
  R20 = Resistor [tolerance=±5% resistance=220 package=THT]  # not connected
  R21 = Resistor [tolerance=±5% resistance=220 package=THT]  # not connected
  R22 = Resistor [tolerance=±5% resistance=220 package=THT]  # not connected
  R23 = Resistor [tolerance=±5% resistance=220 package=THT]  # not connected
  R24 = Resistor [tolerance=±5% resistance=220 package=THT]  # not connected

nets:
  N1: LED5.red_anode, LED7.red_anode, LED8.red_anode, LED13.red_anode, R1.Pin_0
  N2: LED5.blue_anode, LED7.blue_anode, LED8.blue_anode, LED13.blue_anode, R9.Pin_0
  N3: LED5.green_anode, LED7.green_anode, LED8.green_anode, LED13.green_anode, R17.Pin_0
  N4: LED6.red_anode, LED12.red_anode, LED15.red_anode, LED16.red_anode, R2.Pin_0
  N5: LED6.blue_anode, LED12.blue_anode, LED15.blue_anode, LED16.blue_anode, R10.Pin_0
  N6: LED6.green_anode, LED12.green_anode, LED15.green_anode, LED16.green_anode, R18.Pin_0
