# Fritzing sketch conexionadoCompleto (saved by Fritzing 0.9.2b)
breadboards: 1

parts:
  LED1 = RGB LED (com. cathode, rgb) [package="5 mm [THT]"]
  LED2 = RGB LED (com. cathode, rgb) [package="5 mm [THT]"]
  LED4 = RGB LED (com. cathode, rgb) [package="5 mm [THT]"]
  R1 = Resistor [tolerance=±5% resistance=220 package=THT]
  LED33 = RGB LED (com. cathode, rgb) [package="5 mm [THT]"]
  R2 = Resistor [tolerance=±5% resistance=220 package=THT]
  R3 = Resistor [tolerance=±5% resistance=220 package=THT]
  U1 = 74HC595 [package="DIP16 [THT]"]  # not connected
  U2 = 74HC595 [package="DIP16 [THT]"]  # not connected
  U3 = 74HC595 [package="DIP16 [THT]"]  # not connected
  U4 = 74HC595 [package="DIP16 [THT]"]  # not connected
  LED34 = RGB LED (com. cathode, rgb) [package="5 mm [THT]"]
  LED35 = RGB LED (com. cathode, rgb) [package="5 mm [THT]"]
  LED36 = RGB LED (com. cathode, rgb) [package="5 mm [THT]"]
  LED37 = RGB LED (com. cathode, rgb) [package="5 mm [THT]"]
  R4 = Resistor [tolerance=±5% resistance=220 package=THT]
  R5 = Resistor [tolerance=±5% resistance=220 package=THT]
  R6 = Resistor [tolerance=±5% resistance=220 package=THT]
  LED38 = RGB LED (com. cathode, rgb) [package="5 mm [THT]"]
  LED39 = RGB LED (com. cathode, rgb) [package="5 mm [THT]"]
  LED40 = RGB LED (com. cathode, rgb) [package="5 mm [THT]"]
  LED41 = RGB LED (com. cathode, rgb) [package="5 mm [THT]"]
  LED42 = RGB LED (com. cathode, rgb) [package="5 mm [THT]"]
  LED43 = RGB LED (com. cathode, rgb) [package="5 mm [THT]"]
  LED44 = RGB LED (com. cathode, rgb) [package="5 mm [THT]"]
  LED45 = RGB LED (com. cathode, rgb) [package="5 mm [THT]"]
  R7 = Resistor [tolerance=±5% resistance=220 package=THT]
  R8 = Resistor [tolerance=±5% resistance=220 package=THT]
  R9 = Resistor [tolerance=±5% resistance=220 package=THT]
  R10 = Resistor [tolerance=±5% resistance=220 package=THT]
  R11 = Resistor [tolerance=±5% resistance=220 package=THT]
  R12 = Resistor [tolerance=±5% resistance=220 package=THT]
  LED46 = RGB LED (com. cathode, rgb) [package="5 mm [THT]"]
  LED47 = RGB LED (com. cathode, rgb) [package="5 mm [THT]"]
  LED48 = RGB LED (com. cathode, rgb) [package="5 mm [THT]"]
  LED49 = RGB LED (com. cathode, rgb) [package="5 mm [THT]"]
  LED50 = RGB LED (com. cathode, rgb) [package="5 mm [THT]"]
  LED51 = RGB LED (com. cathode, rgb) [package="5 mm [THT]"]
  LED52 = RGB LED (com. cathode, rgb) [package="5 mm [THT]"]
  LED53 = RGB LED (com. cathode, rgb) [package="5 mm [THT]"]
  LED54 = RGB LED (com. cathode, rgb) [package="5 mm [THT]"]
  LED55 = RGB LED (com. cathode, rgb) [package="5 mm [THT]"]
  LED56 = RGB LED (com. cathode, rgb) [package="5 mm [THT]"]
  LED57 = RGB LED (com. cathode, rgb) [package="5 mm [THT]"]
  LED58 = RGB LED (com. cathode, rgb) [package="5 mm [THT]"]
  LED59 = RGB LED (com. cathode, rgb) [package="5 mm [THT]"]
  LED60 = RGB LED (com. cathode, rgb) [package="5 mm [THT]"]
  LED61 = RGB LED (com. cathode, rgb) [package="5 mm [THT]"]
  R13 = Resistor [tolerance=±5% resistance=220 package=THT]
  R14 = Resistor [tolerance=±5% resistance=220 package=THT]
  R15 = Resistor [tolerance=±5% resistance=220 package=THT]
  R16 = Resistor [tolerance=±5% resistance=220 package=THT]
  R17 = Resistor [tolerance=±5% resistance=220 package=THT]
  R18 = Resistor [tolerance=±5% resistance=220 package=THT]
  R19 = Resistor [tolerance=±5% resistance=220 package=THT]
  R20 = Resistor [tolerance=±5% resistance=220 package=THT]
  R21 = Resistor [tolerance=±5% resistance=220 package=THT]
  R22 = Resistor [tolerance=±5% resistance=220 package=THT]
  R23 = Resistor [tolerance=±5% resistance=220 package=THT]
  R24 = Resistor [tolerance=±5% resistance=220 package=THT]

nets:
  N1: LED1.red_anode, LED2.red_anode, LED4.red_anode, LED33.red_anode, R3.Pin_0
  N2: LED1.common_cathode, LED42.common_cathode, LED55.common_cathode, LED58.common_cathode
  N3: LED1.green_anode, LED2.green_anode, LED4.green_anode, R1.Pin_0, LED33.green_anode
  N4: LED1.blue_anode, LED2.blue_anode, LED4.blue_anode, LED33.blue_anode, R2.Pin_0
  N5: LED34.red_anode, LED35.red_anode, LED36.red_anode, LED37.red_anode, R6.Pin_0
  N6: LED34.green_anode, LED35.green_anode, LED36.green_anode, LED37.green_anode, R5.Pin_0
  N7: LED34.blue_anode, LED35.blue_anode, LED36.blue_anode, LED37.blue_anode, R4.Pin_0
  N8: LED37.common_cathode, LED43.common_cathode
  N9: LED38.red_anode, LED39.red_anode, LED40.red_anode, LED42.red_anode, R9.Pin_0
  N10: LED38.green_anode, LED39.green_anode, LED40.green_anode, LED42.green_anode, R10.Pin_0
  N11: LED38.blue_anode, LED39.blue_anode, LED40.blue_anode, LED42.blue_anode, R12.Pin_0
  N12: LED41.red_anode, LED43.red_anode, LED44.red_anode, LED45.red_anode, R8.Pin_0
  N13: LED41.green_anode, LED43.green_anode, LED44.green_anode, LED45.green_anode, R7.Pin_0
  N14: LED41.blue_anode, LED43.blue_anode, LED44.blue_anode, LED45.blue_anode, R11.Pin_0
  N15: LED46.red_anode, LED48.red_anode, LED54.red_anode, LED59.red_anode, R24.Pin_0
  N16: LED46.green_anode, LED48.green_anode, LED54.green_anode, LED59.green_anode, R13.Pin_0
  N17: LED46.blue_anode, LED48.blue_anode, LED54.blue_anode, LED59.blue_anode, R16.Pin_0
  N18: LED47.red_anode, LED51.red_anode, LED57.red_anode, LED58.red_anode, R23.Pin_0
  N19: LED47.green_anode, LED51.green_anode, LED57.green_anode, LED58.green_anode, R17.Pin_0
  N20: LED47.blue_anode, LED51.blue_anode, LED57.blue_anode, LED58.blue_anode, R19.Pin_0
  N21: LED49.red_anode, LED50.red_anode, LED52.red_anode, LED61.red_anode, R18.Pin_0
  N22: LED49.green_anode, LED50.green_anode, LED52.green_anode, LED61.green_anode, R15.Pin_0
  N23: LED49.blue_anode, LED50.blue_anode, LED52.blue_anode, LED61.blue_anode, R22.Pin_0
  N24: LED53.red_anode, LED55.red_anode, LED56.red_anode, LED60.red_anode, R21.Pin_0
  N25: LED53.green_anode, LED55.green_anode, LED56.green_anode, LED60.green_anode, R20.Pin_0
  N26: LED53.blue_anode, LED55.blue_anode, LED56.blue_anode, LED60.blue_anode, R14.Pin_0
