# Fritzing sketch conexionadoRegistros595 (saved by Fritzing 0.9.2b)
breadboards: 1

parts:
  Parte1 = Arduino Uno (Rev3)
  U1 = 74HC595 [package="DIP16 [THT]"]
  U2 = 74HC595 [package="DIP16 [THT]"]
  U3 = 74HC595 [package="DIP16 [THT]"]
  U4 = 74HC595 [package="DIP16 [THT]"]
  R0 = female pin header, 1 pin [form="♀ (female)"]
  R1 = female pin header, 1 pin [form="♀ (female)"]  # not connected
  R2 = female pin header, 1 pin [form="♀ (female)"]
  R3 = female pin header, 1 pin [form="♀ (female)"]
  R4 = female pin header, 1 pin [form="♀ (female)"]
  R5 = female pin header, 1 pin [form="♀ (female)"]
  R6 = female pin header, 1 pin [form="♀ (female)"]
  G1 = female pin header, 1 pin [form="♀ (female)"]
  G2 = female pin header, 1 pin [form="♀ (female)"]
  G3 = female pin header, 1 pin [form="♀ (female)"]
  G4 = female pin header, 1 pin [form="♀ (female)"]
  G5 = female pin header, 1 pin [form="♀ (female)"]
  G6 = female pin header, 1 pin [form="♀ (female)"]
  G7 = female pin header, 1 pin [form="♀ (female)"]
  B1 = female pin header, 1 pin [form="♀ (female)"]  # not connected
  B2 = female pin header, 1 pin [form="♀ (female)"]  # not connected
  B3 = female pin header, 1 pin [form="♀ (female)"]  # not connected
  B4 = female pin header, 1 pin [form="♀ (female)"]  # not connected
  B5 = female pin header, 1 pin [form="♀ (female)"]  # not connected
  B6 = female pin header, 1 pin [form="♀ (female)"]  # not connected
  G0 = female pin header, 1 pin [form="♀ (female)"]
  R7 = female pin header, 1 pin [form="♀ (female)"]  # not connected
  B7 = female pin header, 1 pin [form="♀ (female)"]  # not connected
  B0 = female pin header, 1 pin [form="♀ (female)"]
  C0 = female pin header, 1 pin [form="♀ (female)"]
  C7 = female pin header, 1 pin [form="♀ (female)"]  # not connected
  C6 = female pin header, 1 pin [form="♀ (female)"]  # not connected
  C5 = female pin header, 1 pin [form="♀ (female)"]  # not connected
  C4 = female pin header, 1 pin [form="♀ (female)"]  # not connected
  C3 = female pin header, 1 pin [form="♀ (female)"]  # not connected
  C2 = female pin header, 1 pin [form="♀ (female)"]  # not connected
  C1 = female pin header, 1 pin [form="♀ (female)"]  # not connected

nets:
  N1: Parte1.D8, U1.ST_CP, U2.ST_CP, U3.ST_CP, U4.ST_CP
  N2: Parte1.D11_PWM/MOSI, U1.DS
  N3: Parte1.D12/MISO, U1.SH_CP, U2.SH_CP, U3.SH_CP, U4.SH_CP
  GND: Parte1.GND, U1.GND, U1.OE, U2.GND, U2.OE, U3.GND, U3.OE, U4.GND, U4.OE
  VCC: Parte1.5V, U1.MR, U1.VCC, U2.MR, U2.VCC, U3.MR, U3.VCC, U4.MR, U4.VCC
  N4: U1.Q2, R2.pin1
  N5: U1.Q3, R3.pin1
  N6: U1.Q4, R4.pin1
  N7: U1.Q5, R5.pin1
  N8: U1.Q6, R6.pin1
  N9: U1.Q7', U2.DS
  N10: U1.Q0, R0.pin1
  N11: U2.Q1, G1.pin1
  N12: U2.Q2, G2.pin1
  N13: U2.Q3, G3.pin1
  N14: U2.Q4, G4.pin1
  N15: U2.Q5, G5.pin1
  N16: U2.Q6, G6.pin1
  N17: U2.Q7, G7.pin1
  N18: U2.Q7', U3.DS
  N19: U2.Q0, G0.pin1
  N20: U3.Q7', U4.DS
  N21: U3.Q0, B0.pin1
  N22: U4.Q0, C0.pin1
