# Fritzing sketch cuatroregistros595preparados (saved by Fritzing 0.9.2b)
breadboards: 5

parts:
  LED5 = RGB LED (com. cathode, rbg) [package="5 mm [THT]"]
  LED6 = RGB LED (com. cathode, rbg) [package="5 mm [THT]"]
  LED7 = RGB LED (com. cathode, rbg) [package="5 mm [THT]"]
  LED8 = RGB LED (com. cathode, rbg) [package="5 mm [THT]"]
  LED12 = RGB LED (com. cathode, rbg) [package="5 mm [THT]"]
  LED13 = RGB LED (com. cathode, rbg) [package="5 mm [THT]"]
  LED15 = RGB LED (com. cathode, rbg) [package="5 mm [THT]"]
  LED16 = RGB LED (com. cathode, rbg) [package="5 mm [THT]"]
  R1 = Resistor [tolerance=±5% resistance=220 package=THT]
  R2 = Resistor [tolerance=±5% resistance=220 package=THT]
  R3 = Resistor [tolerance=±5% resistance=220 package=THT]
  R4 = Resistor [tolerance=±5% resistance=220 package=THT]
  R5 = Resistor [tolerance=±5% resistance=220 package=THT]
  R6 = Resistor [tolerance=±5% resistance=220 package=THT]
  R7 = Resistor [tolerance=±5% resistance=220 package=THT]
  R8 = Resistor [tolerance=±5% resistance=220 package=THT]
  R9 = Resistor [tolerance=±5% resistance=220 package=THT]
  R10 = Resistor [tolerance=±5% resistance=220 package=THT]
  R11 = Resistor [tolerance=±5% resistance=220 package=THT]
  R12 = Resistor [tolerance=±5% resistance=220 package=THT]
  R13 = Resistor [tolerance=±5% resistance=220 package=THT]
  R14 = Resistor [tolerance=±5% resistance=220 package=THT]
  R15 = Resistor [tolerance=±5% resistance=220 package=THT]
  R16 = Resistor [tolerance=±5% resistance=220 package=THT]
  R17 = Resistor [tolerance=±5% resistance=220 package=THT]
  R18 = Resistor [tolerance=±5% resistance=220 package=THT]
  R19 = Resistor [tolerance=±5% resistance=220 package=THT]
  R20 = Resistor [tolerance=±5% resistance=220 package=THT]
  R21 = Resistor [tolerance=±5% resistance=220 package=THT]
  R22 = Resistor [tolerance=±5% resistance=220 package=THT]
  R23 = Resistor [tolerance=±5% resistance=220 package=THT]
  R24 = Resistor [tolerance=±5% resistance=220 package=THT]
  LED33 = RGB LED (com. cathode, rbg) [package="5 mm [THT]"]
  LED34 = RGB LED (com. cathode, rbg) [package="5 mm [THT]"]
  LED35 = RGB LED (com. cathode, rbg) [package="5 mm [THT]"]
  LED36 = RGB LED (com. cathode, rbg) [package="5 mm [THT]"]
  LED37 = RGB LED (com. cathode, rbg) [package="5 mm [THT]"]
  LED38 = RGB LED (com. cathode, rbg) [package="5 mm [THT]"]
  LED39 = RGB LED (com. cathode, rbg) [package="5 mm [THT]"]
  LED40 = RGB LED (com. cathode, rbg) [package="5 mm [THT]"]
  LED41 = RGB LED (com. cathode, rbg) [package="5 mm [THT]"]
  LED42 = RGB LED (com. cathode, rbg) [package="5 mm [THT]"]
  LED43 = RGB LED (com. cathode, rbg) [package="5 mm [THT]"]
  LED44 = RGB LED (com. cathode, rbg) [package="5 mm [THT]"]
  LED45 = RGB LED (com. cathode, rbg) [package="5 mm [THT]"]
  LED46 = RGB LED (com. cathode, rbg) [package="5 mm [THT]"]
  LED47 = RGB LED (com. cathode, rbg) [package="5 mm [THT]"]
  LED48 = RGB LED (com. cathode, rbg) [package="5 mm [THT]"]
  LED49 = RGB LED (com. cathode, rbg) [package="5 mm [THT]"]
  LED50 = RGB LED (com. cathode, rbg) [package="5 mm [THT]"]
  LED51 = RGB LED (com. cathode, rbg) [package="5 mm [THT]"]
  LED52 = RGB LED (com. cathode, rbg) [package="5 mm [THT]"]
  LED53 = RGB LED (com. cathode, rbg) [package="5 mm [THT]"]
  LED54 = RGB LED (com. cathode, rbg) [package="5 mm [THT]"]
  LED55 = RGB LED (com. cathode, rbg) [package="5 mm [THT]"]
  LED56 = RGB LED (com. cathode, rbg) [package="5 mm [THT]"]
  U1 = 74HC595 [package="DIP16 [THT]"]
  Parte1 = Arduino Uno (Rev3)
  U2 = 74HC595 [package="DIP16 [THT]"]
  U3 = 74HC595 [package="DIP16 [THT]"]
  U4 = 74HC595 [package="DIP16 [THT]"]

nets:
  N1: LED5.red_anode, LED7.red_anode, LED8.red_anode, LED13.red_anode, R1.Pin_0
  N2: LED5.common_cathode, LED40.common_cathode, LED48.common_cathode, LED56.common_cathode
  N3: LED5.blue_anode, LED7.blue_anode, LED8.blue_anode, LED13.blue_anode, R9.Pin_0
  N4: LED5.green_anode, LED7.green_anode, LED8.green_anode, LED13.green_anode, R17.Pin_0
  N5: LED6.red_anode, LED12.red_anode, LED15.red_anode, LED16.red_anode, R2.Pin_0
  N6: LED6.common_cathode, LED39.common_cathode, LED47.common_cathode, LED55.common_cathode
  N7: LED6.blue_anode, LED12.blue_anode, LED15.blue_anode, LED16.blue_anode, R10.Pin_0
  N8: LED6.green_anode, LED12.green_anode, LED15.green_anode, LED16.green_anode, R18.Pin_0
  N9: LED7.common_cathode, LED38.common_cathode, LED46.common_cathode, LED54.common_cathode
  N10: LED8.common_cathode, LED37.common_cathode, LED45.common_cathode, LED53.common_cathode
  N11: LED12.common_cathode, LED36.common_cathode, LED44.common_cathode, LED52.common_cathode
  N12: LED13.common_cathode, LED35.common_cathode, LED43.common_cathode, LED51.common_cathode
  N13: LED15.common_cathode, LED34.common_cathode, LED42.common_cathode, LED50.common_cathode
  N14: LED16.common_cathode, LED33.common_cathode, LED41.common_cathode, LED49.common_cathode
  N15: R3.Pin_0, LED33.red_anode, LED34.red_anode, LED36.red_anode, LED39.red_anode
  N16: R4.Pin_0, LED35.red_anode, LED37.red_anode, LED38.red_anode, LED40.red_anode
  N17: R5.Pin_0, LED41.red_anode, LED42.red_anode, LED44.red_anode, LED47.red_anode
  N18: R6.Pin_0, LED43.red_anode, LED45.red_anode, LED46.red_anode, LED48.red_anode
  N19: R7.Pin_0, LED49.red_anode, LED50.red_anode, LED52.red_anode, LED55.red_anode
  N20: R8.Pin_0, LED51.red_anode, LED53.red_anode, LED54.red_anode, LED56.red_anode
  N21: R11.Pin_0, LED33.blue_anode, LED34.blue_anode, LED36.blue_anode, LED39.blue_anode
  N22: R12.Pin_0, LED35.blue_anode, LED37.blue_anode, LED38.blue_anode, LED40.blue_anode
  N23: R13.Pin_0, LED41.blue_anode, LED42.blue_anode, LED44.blue_anode, LED47.blue_anode
  N24: R14.Pin_0, LED43.blue_anode, LED45.blue_anode, LED46.blue_anode, LED48.blue_anode
  N25: R15.Pin_0, LED49.blue_anode, LED50.blue_anode, LED52.blue_anode, LED55.blue_anode
  N26: R16.Pin_0, LED51.blue_anode, LED53.blue_anode, LED54.blue_anode, LED56.blue_anode
  N27: R19.Pin_0, LED33.green_anode, LED34.green_anode, LED36.green_anode, LED39.green_anode
  N28: R20.Pin_0, LED35.green_anode, LED37.green_anode, LED38.green_anode, LED40.green_anode
  N29: R21.Pin_0, LED41.green_anode, LED42.green_anode, LED44.green_anode, LED47.green_anode
  N30: R22.Pin_0, LED43.green_anode, LED45.green_anode, LED46.green_anode, LED48.green_anode
  N31: R23.Pin_0, LED49.green_anode, LED50.green_anode, LED52.green_anode, LED55.green_anode
  N32: R24.Pin_0, LED51.green_anode, LED53.green_anode, LED54.green_anode, LED56.green_anode
  GND: U1.GND, U1.OE, Parte1.GND, U2.GND, U2.OE, U3.GND, U3.OE, U4.GND, U4.OE
  N33: U1.Q7', U2.DS
  VCC: U1.MR, U1.VCC, Parte1.5V, U2.MR, U2.VCC, U3.MR, U3.VCC, U4.MR, U4.VCC
  N34: U1.SH_CP, Parte1.D12/MISO, U2.SH_CP, U3.SH_CP, U4.SH_CP
  N35: U1.ST_CP, Parte1.D8, U2.ST_CP, U3.ST_CP, U4.ST_CP
  N36: U1.DS, Parte1.D11_PWM/MOSI
  N37: U2.Q7', U3.DS
  N38: U3.Q7', U4.DS
