# Fritzing sketch esquemaMatrizLeds (saved by Fritzing 0.9.2b)
breadboards: 1

parts:
  LED1 = RGB LED (com. cathode, rgb) [package="5 mm [THT]"]
  LED2 = RGB LED (com. cathode, rgb) [package="5 mm [THT]"]
  LED4 = RGB LED (com. cathode, rgb) [package="5 mm [THT]"]
  R0 = Resistor [tolerance=±5% resistance=220 package=THT]
  LED33 = RGB LED (com. cathode, rgb) [package="5 mm [THT]"]
  G0 = Resistor [tolerance=±5% resistance=220 package=THT]
  B0 = Resistor [tolerance=±5% resistance=220 package=THT]
  LED34 = RGB LED (com. cathode, rgb) [package="5 mm [THT]"]
  LED35 = RGB LED (com. cathode, rgb) [package="5 mm [THT]"]
  LED36 = RGB LED (com. cathode, rgb) [package="5 mm [THT]"]
  LED37 = RGB LED (com. cathode, rgb) [package="5 mm [THT]"]
  G1 = Resistor [tolerance=±5% resistance=220 package=THT]
  R1 = Resistor [tolerance=±5% resistance=220 package=THT]
  B1 = Resistor [tolerance=±5% resistance=220 package=THT]
  LED38 = RGB LED (com. cathode, rgb) [package="5 mm [THT]"]
  LED39 = RGB LED (com. cathode, rgb) [package="5 mm [THT]"]
  LED40 = RGB LED (com. cathode, rgb) [package="5 mm [THT]"]
  LED41 = RGB LED (com. cathode, rgb) [package="5 mm [THT]"]
  LED42 = RGB LED (com. cathode, rgb) [package="5 mm [THT]"]
  LED43 = RGB LED (com. cathode, rgb) [package="5 mm [THT]"]
  LED44 = RGB LED (com. cathode, rgb) [package="5 mm [THT]"]
  LED45 = RGB LED (com. cathode, rgb) [package="5 mm [THT]"]
  R3 = Resistor [tolerance=±5% resistance=220 package=THT]
  B3 = Resistor [tolerance=±5% resistance=220 package=THT]
  B2 = Resistor [tolerance=±5% resistance=220 package=THT]
  R2 = Resistor [tolerance=±5% resistance=220 package=THT]
  G3 = Resistor [tolerance=±5% resistance=220 package=THT]
  G2 = Resistor [tolerance=±5% resistance=220 package=THT]
  LED46 = RGB LED (com. cathode, rgb) [package="5 mm [THT]"]
  LED47 = RGB LED (com. cathode, rgb) [package="5 mm [THT]"]
  LED48 = RGB LED (com. cathode, rgb) [package="5 mm [THT]"]
  LED49 = RGB LED (com. cathode, rgb) [package="5 mm [THT]"]
  LED50 = RGB LED (com. cathode, rgb) [package="5 mm [THT]"]
  LED51 = RGB LED (com. cathode, rgb) [package="5 mm [THT]"]
  LED52 = RGB LED (com. cathode, rgb) [package="5 mm [THT]"]
  LED53 = RGB LED (com. cathode, rgb) [package="5 mm [THT]"]
  LED54 = RGB LED (com. cathode, rgb) [package="5 mm [THT]"]
  LED55 = RGB LED (com. cathode, rgb) [package="5 mm [THT]"]
  LED56 = RGB LED (com. cathode, rgb) [package="5 mm [THT]"]
  LED57 = RGB LED (com. cathode, rgb) [package="5 mm [THT]"]
  LED58 = RGB LED (com. cathode, rgb) [package="5 mm [THT]"]
  LED59 = RGB LED (com. cathode, rgb) [package="5 mm [THT]"]
  LED60 = RGB LED (com. cathode, rgb) [package="5 mm [THT]"]
  LED61 = RGB LED (com. cathode, rgb) [package="5 mm [THT]"]
  R5 = Resistor [tolerance=±5% resistance=220 package=THT]
  G6 = Resistor [tolerance=±5% resistance=220 package=THT]
  R7 = Resistor [tolerance=±5% resistance=220 package=THT]
  G5 = Resistor [tolerance=±5% resistance=220 package=THT]
  R4 = Resistor [tolerance=±5% resistance=220 package=THT]
  B7 = Resistor [tolerance=±5% resistance=220 package=THT]
  G4 = Resistor [tolerance=±5% resistance=220 package=THT]
  R6 = Resistor [tolerance=±5% resistance=220 package=THT]
  B6 = Resistor [tolerance=±5% resistance=220 package=THT]
  G7 = Resistor [tolerance=±5% resistance=220 package=THT]
  B4 = Resistor [tolerance=±5% resistance=220 package=THT]
  B5 = Resistor [tolerance=±5% resistance=220 package=THT]
  C0 = female pin header, 1 pin [form="♀ (female)"]
  C1 = female pin header, 1 pin [form="♀ (female)"]
  C2 = female pin header, 1 pin [form="♀ (female)"]
  C3 = female pin header, 1 pin [form="♀ (female)"]
  C4 = female pin header, 1 pin [form="♀ (female)"]
  C5 = female pin header, 1 pin [form="♀ (female)"]
  C7 = female pin header, 1 pin [form="♀ (female)"]
  C6 = female pin header, 1 pin [form="♀ (female)"]  # not connected

nets:
  N1: LED1.red_anode, LED2.red_anode, LED4.red_anode, LED33.red_anode, B0.Pin_0
  N2: LED1.common_cathode, LED42.common_cathode, LED55.common_cathode, LED58.common_cathode, C0.pin1
  N3: LED1.green_anode, LED2.green_anode, LED4.green_anode, R0.Pin_0, LED33.green_anode
  N4: LED1.blue_anode, LED2.blue_anode, LED4.blue_anode, LED33.blue_anode, G0.Pin_0
  N5: LED2.common_cathode, LED38.common_cathode
  N6: LED4.common_cathode, LED40.common_cathode, LED57.common_cathode, LED60.common_cathode, C4.pin1
  N7: LED33.common_cathode, LED39.common_cathode, LED51.common_cathode, LED56.common_cathode
  N8: LED34.red_anode, LED35.red_anode, LED36.red_anode, LED37.red_anode, B1.Pin_0
  N9: LED34.common_cathode, LED45.common_cathode, LED48.common_cathode, LED52.common_cathode, C3.pin1
  N10: LED34.green_anode, LED35.green_anode, LED36.green_anode, LED37.green_anode, R1.Pin_0
  N11: LED34.blue_anode, LED35.blue_anode, LED36.blue_anode, LED37.blue_anode, G1.Pin_0
  N12: LED35.common_cathode, LED41.common_cathode, LED49.common_cathode, LED59.common_cathode, C5.pin1
  N13: LED36.common_cathode, LED44.common_cathode, LED54.common_cathode, LED61.common_cathode, C7.pin1
  N14: LED37.common_cathode, LED43.common_cathode, LED46.common_cathode, LED50.common_cathode, C1.pin1
  N15: LED38.red_anode, LED39.red_anode, LED40.red_anode, LED42.red_anode, B2.Pin_0
  N16: LED38.green_anode, LED39.green_anode, LED40.green_anode, LED42.green_anode, R2.Pin_0
  N17: LED38.blue_anode, LED39.blue_anode, LED40.blue_anode, LED42.blue_anode, G2.Pin_0
  N18: LED41.red_anode, LED43.red_anode, LED44.red_anode, LED45.red_anode, B3.Pin_0
  N19: LED41.green_anode, LED43.green_anode, LED44.green_anode, LED45.green_anode, R3.Pin_0
  N20: LED41.blue_anode, LED43.blue_anode, LED44.blue_anode, LED45.blue_anode, G3.Pin_0
  N21: LED46.red_anode, LED48.red_anode, LED54.red_anode, LED59.red_anode, B5.Pin_0
  N22: LED46.green_anode, LED48.green_anode, LED54.green_anode, LED59.green_anode, R5.Pin_0
  N23: LED46.blue_anode, LED48.blue_anode, LED54.blue_anode, LED59.blue_anode, G5.Pin_0
  N24: LED47.red_anode, LED51.red_anode, LED57.red_anode, LED58.red_anode, B4.Pin_0
  N25: LED47.common_cathode, LED53.common_cathode, C2.pin1
  N26: LED47.green_anode, LED51.green_anode, LED57.green_anode, LED58.green_anode, R4.Pin_0
  N27: LED47.blue_anode, LED51.blue_anode, LED57.blue_anode, LED58.blue_anode, G4.Pin_0
  N28: LED49.red_anode, LED50.red_anode, LED52.red_anode, LED61.red_anode, B7.Pin_0
  N29: LED49.green_anode, LED50.green_anode, LED52.green_anode, LED61.green_anode, R7.Pin_0
  N30: LED49.blue_anode, LED50.blue_anode, LED52.blue_anode, LED61.blue_anode, G7.Pin_0
  N31: LED53.red_anode, LED55.red_anode, LED56.red_anode, LED60.red_anode, B6.Pin_0
  N32: LED53.green_anode, LED55.green_anode, LED56.green_anode, LED60.green_anode, R6.Pin_0
  N33: LED53.blue_anode, LED55.blue_anode, LED56.blue_anode, LED60.blue_anode, G6.Pin_0
