# Fritzing sketch registros595 (saved by Fritzing 0.8.5b)
breadboards: 2

parts:
  U1 = 74HC595 [package="DIP16 [THT]"]
  U2 = 74HC595 [package="DIP16 [THT]"]
  U3 = 74HC595 [package="DIP16 [THT]"]
  U4 = 74HC595 [package="DIP16 [THT]"]

nets:
  GND: U1.GND, U1.OE, U2.GND, U2.OE, U3.GND, U4.GND, U4.OE
  N1: U1.Q7', U3.DS
  VCC: U1.MR, U1.VCC, U2.MR, U2.VCC, U3.MR, U3.VCC, U4.MR, U4.DS, U4.VCC
  N2: U1.SH_CP, U1.ST_CP, U2.SH_CP, U2.ST_CP, U3.SH_CP, U3.ST_CP, U4.SH_CP
  N3: U1.DS, U2.Q7'

notes:
  Patilla 11 de Arduino
  Azul
  Verde
  Columnas
  Rojo
  Patilla 12 de Arduino
  Patilla 8 de Arduino
