# Fritzing sketch rojoconDiodos (saved by Fritzing 0.8.5b)
breadboards: 2

parts:
  LED1 = RGB LED (com. cathode, rgb) [package="5 mm [THT]"]  # not connected
  LED2 = RGB LED (com. cathode, rgb) [package="5 mm [THT]"]
  LED3 = RGB LED (com. cathode, rgb) [package="5 mm [THT]"]
  LED4 = RGB LED (com. cathode, rgb) [package="5 mm [THT]"]
  LED5 = RGB LED (com. cathode, rgb) [package="5 mm [THT]"]
  LED6 = RGB LED (com. cathode, rgb) [package="5 mm [THT]"]
  LED7 = RGB LED (com. cathode, rgb) [package="5 mm [THT]"]
  LED8 = RGB LED (com. cathode, rgb) [package="5 mm [THT]"]
  LED10 = RGB LED (com. cathode, rgb) [package="5 mm [THT]"]
  LED11 = RGB LED (com. cathode, rgb) [package="5 mm [THT]"]
  LED12 = RGB LED (com. cathode, rgb) [package="5 mm [THT]"]
  LED13 = RGB LED (com. cathode, rgb) [package="5 mm [THT]"]
  LED14 = RGB LED (com. cathode, rgb) [package="5 mm [THT]"]
  LED15 = RGB LED (com. cathode, rgb) [package="5 mm [THT]"]
  LED16 = RGB LED (com. cathode, rgb) [package="5 mm [THT]"]
  LED17 = RGB LED (com. cathode, rgb) [package="5 mm [THT]"]
  LED18 = RGB LED (com. cathode, rgb) [package="5 mm [THT]"]
  LED19 = RGB LED (com. cathode, rgb) [package="5 mm [THT]"]
  LED20 = RGB LED (com. cathode, rgb) [package="5 mm [THT]"]
  LED21 = RGB LED (com. cathode, rgb) [package="5 mm [THT]"]
  LED22 = RGB LED (com. cathode, rgb) [package="5 mm [THT]"]
  LED23 = RGB LED (com. cathode, rgb) [package="5 mm [THT]"]
  LED24 = RGB LED (com. cathode, rgb) [package="5 mm [THT]"]
  LED25 = RGB LED (com. cathode, rgb) [package="5 mm [THT]"]
  LED26 = RGB LED (com. cathode, rgb) [package="5 mm [THT]"]
  LED27 = RGB LED (com. cathode, rgb) [package="5 mm [THT]"]
  LED28 = RGB LED (com. cathode, rgb) [package="5 mm [THT]"]
  LED29 = RGB LED (com. cathode, rgb) [package="5 mm [THT]"]
  LED30 = RGB LED (com. cathode, rgb) [package="5 mm [THT]"]
  U1 = 74HC595 [package="DIP16 [THT]"]
  U2 = 74HC595 [package="DIP16 [THT]"]  # not connected
  U3 = 74HC595 [package="DIP16 [THT]"]  # not connected
  U4 = 74HC595 [package="DIP16 [THT]"]  # not connected
  R1 = Resistor [tolerance=±5% resistance=220 package=THT]
  R2 = Resistor [tolerance=±5% resistance=220 package=THT]
  R3 = Resistor [tolerance=±5% resistance=220 package=THT]
  R4 = Resistor [tolerance=±5% resistance=220 package=THT]
  R5 = Resistor [tolerance=±5% resistance=220 package=THT]
  R6 = Resistor [tolerance=±5% resistance=220 package=THT]
  R7 = Resistor [tolerance=±5% resistance=220 package=THT]

nets:
  N1: LED2.red_anode, LED3.red_anode, LED7.red_anode, LED8.red_anode, R2.Pin_1
  N2: LED4.red_anode, LED5.red_anode, LED6.red_anode, R1.Pin_0
  N3: LED10.red_anode, LED13.red_anode, LED14.red_anode
  N4: LED11.red_anode, LED12.red_anode, LED15.red_anode, R3.Pin_0
  N5: LED16.red_anode, LED17.red_anode, LED24.red_anode, LED26.red_anode, R5.Pin_1
  N6: LED18.red_anode, LED22.red_anode, LED28.red_anode, LED29.red_anode, R7.Pin_1
  N7: LED19.red_anode, LED21.red_anode, LED27.red_anode, R6.Pin_1
  N8: LED20.red_anode, LED23.red_anode, LED25.red_anode, LED30.red_anode, R4.Pin_1
  N9: U1.Q3, R3.Pin_1
  N10: U1.Q4, R4.Pin_0
  N11: U1.Q5, R5.Pin_0
  N12: U1.Q6, R6.Pin_0
  N13: U1.Q7, R7.Pin_0
  N14: U1.Q0, R1.Pin_1
