# Fritzing sketch rojosinDiodos (saved by Fritzing 0.8.5b)
breadboards: 2

parts:
  U1 = 74HC595 [package="DIP16 [THT]"]
  U2 = 74HC595 [package="DIP16 [THT]"]  # not connected
  U3 = 74HC595 [package="DIP16 [THT]"]  # not connected
  U4 = 74HC595 [package="DIP16 [THT]"]  # not connected
  R1 = Resistor [tolerance=±5% resistance=220 package=THT]
  R2 = Resistor [tolerance=±5% resistance=220 package=THT]  # not connected
  R3 = Resistor [tolerance=±5% resistance=220 package=THT]
  R4 = Resistor [tolerance=±5% resistance=220 package=THT]
  R5 = Resistor [tolerance=±5% resistance=220 package=THT]
  R6 = Resistor [tolerance=±5% resistance=220 package=THT]
  R7 = Resistor [tolerance=±5% resistance=220 package=THT]

nets:
  N1: U1.Q3, R3.Pin_1
  N2: U1.Q4, R4.Pin_0
  N3: U1.Q5, R5.Pin_0
  N4: U1.Q6, R6.Pin_0
  N5: U1.Q7, R7.Pin_0
  N6: U1.Q0, R1.Pin_1
