# Fritzing sketch sketchFritzing (saved by Fritzing 0.9.2b)
breadboards: 1

parts:
  R1 = Resistor [tolerance=±5% resistance=220 package=THT]
  R2 = Resistor [tolerance=±5% resistance=220 package=THT]
  LEDDerecha = LED - 5mm [color="Red (633nm)" package="5 mm [THT]"]
  R3 = Rotary Potentiometer (Small) [maximum_resistance=10kΩ package=THT]
  sDerecha = Photocell (LDR) [package=THT]
  R4 = Rotary Potentiometer (Small) [maximum_resistance=10kΩ package=THT]
  Parte1 = Arduino Uno (Rev3)
  LEDDerecha1 = LED - 5mm [color="Red (633nm)" package="5 mm [THT]"]
  sDerecha1 = Photocell (LDR) [package=THT]

nets:
  N1: R1.Pin_0, Parte1.D9_PWM
  N2: R1.Pin_1, LEDDerecha.anode
  N3: R2.Pin_0, LEDDerecha1.anode
  N4: R2.Pin_1, Parte1.D8
  N5: LEDDerecha.cathode, sDerecha.pin_1, Parte1.GND, LEDDerecha1.cathode, sDerecha1.pin_1
  N6: R3.leg1, R4.leg1, Parte1.5V
  N7: R3.wiper, Parte1.A1, sDerecha1.pin_0
  N8: sDerecha.pin_0, R4.wiper, Parte1.A0
