# Fritzing sketch esquemaConexiones (saved by Fritzing 0.9.2b)
breadboards: 1

parts:
  Parte1 = Arduino Uno (Rev3)
  LED1 = RGB LED (com. cathode, rgb) [package="5 mm [THT]"]
  R1 = Rotary Potentiometer (Small) [maximum_resistance=100kΩ package=THT]
  R2 = Rotary Potentiometer (Small) [maximum_resistance=100kΩ package=THT]
  R3 = Rotary Potentiometer (Small) [maximum_resistance=100kΩ package=THT]

nets:
  N1: Parte1.A0, R1.wiper
  N2: Parte1.A1, R2.wiper
  N3: Parte1.A2, R3.wiper
  N4: Parte1.D9_PWM, LED1.red_anode
  N5: Parte1.D10_PWM/SS, LED1.common_cathode
  N6: Parte1.D11_PWM/MOSI, LED1.blue_anode
  N7: Parte1.GND, LED1.green_anode, R1.leg2, R2.leg2, R3.leg2
  N8: Parte1.5V, R1.leg1, R2.leg1, R3.leg1
