# Fritzing sketch EsquemaControl (saved by Fritzing 0.9.2b)
breadboards: 1

parts:
  R1 = Rotary Potentiometer (Small) [maximum_resistance=100kΩ package=THT]
  LED1 = LED - 5mm [color="Red (633nm)" package="5 mm [THT]"]
  R2 = Photocell (LDR) [package=THT]
  Parte1 = Arduino Uno (Rev3)

nets:
  N1: R1.wiper, Parte1.5V
  N2: R1.leg2, R2.pin_0, Parte1.A0
  N3: LED1.cathode, R2.pin_1, Parte1.GND
  N4: LED1.anode, Parte1.D8
