# Fritzing sketch EsquemaPotencia (saved by Fritzing 0.9.2b)
breadboards: 1

parts:
  R1 = Rotary Potentiometer (Small) [maximum_resistance=100kΩ package=THT]
  R2 = Photocell (LDR) [package=THT]
  Parte1 = Arduino Uno (Rev3)
  K1 = Relay [part_number=FRS1B-S package=THT]
  J1 = Screw terminal - 2 pins [package=THT]
  J2 = Screw terminal - 2 pins [package=THT]

nets:
  N1: R1.wiper, Parte1.5V
  N2: R1.leg2, R2.pin_0, Parte1.A0
  N3: R2.pin_1, Parte1.GND, K1.COIL1
  N4: Parte1.D8, K1.COIL2
  N5: K1.A, J2.pin2
  N6: K1.C1, K1.C2, J1.pin1
  N7: J1.pin2, J2.pin1

notes:
  ALIMENTACIÓN O ENCHUFE
  AL/LOS PORTALÁMPARAS
  ENCHUFE
  BOMBILLA
