# Fritzing sketch controlRGBporBT (saved by Fritzing 0.9.2b)
breadboards: 1

parts:
  Part3 = Bluetooth Mate Silver
  Parte1 = Arduino Uno (Rev3)
  R1 = Resistor [tolerance=±5% resistance=220 package=THT]
  R2 = Resistor [tolerance=±5% resistance=220 package=THT]
  R3 = Resistor [tolerance=±5% resistance=220 package=THT]
  LED1 = RGB LED - (4 legs) [package="5 mm [THT]"]

nets:
  N1: Part3.RX_5V, R1.Pin_1, R2.Pin_0
  N2: Part3.TX_5V, Parte1.D6_PWM
  N3: Part3.VCC, R3.Pin_1, LED1.common_anode
  N4: Part3.CTS_5V, Part3.GND
  N5: Parte1.D8, LED1.red_cathode
  N6: Parte1.D9_PWM, LED1.green_cathode
  N7: Parte1.D10_PWM/SS, LED1.blue_cathode
  N8: Parte1.D7, R1.Pin_0
  N9: R2.Pin_1, R3.Pin_0

notes:
  XXXXXX
  RXD
  TXD
  GND
  VCC
  JY-MCU
  V1.05
  5 VCC
