# Fritzing sketch HC595BASICS (saved by Fritzing 0.9.2b)
breadboards: 1

parts:
  U1 = 74HC595 SMD [package="SO16 [SMD]"]
  Parte1 = Arduino Uno (Rev3)

nets:
  GND: U1.GND, U1.OE, Parte1.GND
  VCC: U1.MR, U1.VCC, Parte1.5V

notes:
  PIN 8->GND
  PIN 16->VCC
  PIN 13(OE)->GND
  PIN 10 (MR)->VCC
