# Fritzing sketch montaje595a8ledscompleto (saved by Fritzing 0.9.2b)
breadboards: 1

parts:
  LED1 = LED - 5mm [color="Red (633nm)" package="5 mm [THT]"]
  LED2 = LED - 5mm [color="Red (633nm)" package="5 mm [THT]"]
  LED3 = LED - 5mm [color="Red (633nm)" package="5 mm [THT]"]
  LED4 = LED - 5mm [color="Red (633nm)" package="5 mm [THT]"]
  LED5 = LED - 5mm [color="Red (633nm)" package="5 mm [THT]"]
  LED6 = LED - 5mm [color="Red (633nm)" package="5 mm [THT]"]
  LED7 = LED - 5mm [color="Red (633nm)" package="5 mm [THT]"]
  LED8 = LED - 5mm [color="Red (633nm)" package="5 mm [THT]"]
  Parte1 = Arduino Uno (Rev3)
  U1 = 74HC595 SMD [package="SO16 [SMD]"]
  R1 = Resistor [tolerance=±5% resistance=220 package=THT]
  R2 = Resistor [tolerance=±5% resistance=220 package=THT]
  R3 = Resistor [tolerance=±5% resistance=220 package=THT]
  R4 = Resistor [tolerance=±5% resistance=220 package=THT]
  R5 = Resistor [tolerance=±5% resistance=220 package=THT]
  R6 = Resistor [tolerance=±5% resistance=220 package=THT]
  R7 = Resistor [tolerance=±5% resistance=220 package=THT]
  R8 = Resistor [tolerance=±5% resistance=220 package=THT]

nets:
  GND: LED1.cathode, LED2.cathode, LED3.cathode, LED4.cathode, LED5.cathode, LED6.cathode, LED7.cathode, LED8.cathode, Parte1.GND, U1.GND, U1.OE
  N1: LED1.anode, R1.Pin_1
  N2: LED2.anode, R2.Pin_1
  N3: LED3.anode, R3.Pin_1
  N4: LED4.anode, R4.Pin_1
  N5: LED5.anode, R5.Pin_1
  N6: LED6.anode, R6.Pin_1
  N7: LED7.anode, R7.Pin_1
  N8: LED8.anode, R8.Pin_1
  N9: Parte1.D8, U1.ST_CP
  N10: Parte1.D11_PWM/MOSI, U1.DS
  N11: Parte1.D12/MISO, U1.SH_CP
  5V: Parte1.5V, U1.MR, U1.VCC
  N12: U1.Q1, R7.Pin_0
  N13: U1.Q2, R6.Pin_0
  N14: U1.Q3, R5.Pin_0
  N15: U1.Q4, R4.Pin_0
  N16: U1.Q5, R3.Pin_0
  N17: U1.Q6, R2.Pin_0
  N18: U1.Q7, R1.Pin_0
  N19: U1.Q0, R8.Pin_0

notes:
  Ahora sólo utilizamos un pin de Arduino como entrada al 74595
  El 74595 conecta sus 8 salidas a los leds
