# Fritzing sketch montajeElectronico (saved by Fritzing 0.9.2b)
breadboards: 1

parts:
  J1 = female pin header, 1 pin [form="♀ (female)"]
  LED1 = LED - 5mm [color="Red (633nm)" package="5 mm [THT]"]
  LED2 = LED - 5mm [color="Red (633nm)" package="5 mm [THT]"]
  LED3 = LED - 5mm [color="Red (633nm)" package="5 mm [THT]"]
  LED4 = LED - 5mm [color="Red (633nm)" package="5 mm [THT]"]
  LED5 = LED - 5mm [color="Red (633nm)" package="5 mm [THT]"]
  LED6 = LED - 5mm [color="Red (633nm)" package="5 mm [THT]"]
  LED7 = LED - 5mm [color="Red (633nm)" package="5 mm [THT]"]
  LED8 = LED - 5mm [color="Red (633nm)" package="5 mm [THT]"]
  LED9 = LED - 5mm [color="Red (633nm)" package="5 mm [THT]"]
  LED10 = LED - 5mm [color="Red (633nm)" package="5 mm [THT]"]
  LED11 = LED - 5mm [color="Red (633nm)" package="5 mm [THT]"]
  LED12 = LED - 5mm [color="Red (633nm)" package="5 mm [THT]"]
  LED13 = LED - 5mm [color="Red (633nm)" package="5 mm [THT]"]
  LED14 = LED - 5mm [color="Red (633nm)" package="5 mm [THT]"]
  LED15 = LED - 5mm [color="Red (633nm)" package="5 mm [THT]"]
  LED16 = LED - 5mm [color="Red (633nm)" package="5 mm [THT]"]
  J2 = female pin header, 1 pin [form="♀ (female)"]
  J3 = female pin header, 1 pin [form="♀ (female)"]
  J4 = female pin header, 1 pin [form="♀ (female)"]
  J5 = female pin header, 1 pin [form="♀ (female)"]
  J6 = female pin header, 1 pin [form="♀ (female)"]
  J7 = female pin header, 1 pin [form="♀ (female)"]
  J8 = female pin header, 1 pin [form="♀ (female)"]

nets:
  N1: J1.pin1, LED3.anode, LED8.anode, LED12.anode, LED16.anode
  N2: LED1.cathode, LED5.cathode, LED9.cathode, LED13.cathode, J8.pin1
  N3: LED1.anode, LED5.anode, LED9.anode, LED13.anode, J4.pin1
  N4: LED2.cathode, LED7.cathode, LED11.cathode, LED15.cathode, J7.pin1
  N5: LED2.anode, LED7.anode, LED11.anode, LED15.anode, J3.pin1
  N6: LED3.cathode, LED8.cathode, LED12.cathode, LED16.cathode, J6.pin1
  N7: LED4.cathode, LED6.cathode, LED10.cathode, LED14.cathode, J5.pin1
  N8: LED4.anode, LED6.anode, LED10.anode, LED14.anode, J2.pin1
