# Fritzing sketch proyectoCajaFuerte (saved by Fritzing 0.8.5b)
breadboards: 1

parts:
  Parte1 = Arduino Uno (Rev3)
  R1 = Resistor [tolerance=±5% resistance=220 package=THT]
  R2 = Resistor [tolerance=±5% resistance=220 package=THT]
  R3 = Resistor [tolerance=±5% resistance=220 package=THT]
  R4 = Resistor [tolerance=±5% resistance=220 package=THT]
  S1 = Pushbutton [package="[THT]"]
  S2 = Pushbutton [package="[THT]"]
  S3 = Pushbutton [package="[THT]"]
  S4 = Pushbutton [package="[THT]"]
  R5 = Resistor [tolerance=±5% resistance=220 package=THT]
  S5 = Pushbutton [package="[THT]"]
  LED1 = LED - 5mm [color="Red (633nm)" package="5 mm [THT]"]  # not connected
  LED2 = LED - 5mm [color="Green (565nm)" package="5 mm [THT]"]  # not connected
  J1 = Piezo Speaker
  J2 = Basic Servo

nets:
  N1: Parte1.D8, R3.Pin_0, S3.Pin_1, S3.Pin_2
  N2: Parte1.D9_PWM, R2.Pin_0, S2.Pin_1, S2.Pin_2
  N3: Parte1.D10_PWM/SS, R1.Pin_0, S1.Pin_1, S1.Pin_2
  N4: Parte1.D11_PWM/MOSI, R5.Pin_0, S5.Pin_1, S5.Pin_2
  N5: Parte1.D12/MISO, R4.Pin_0
  N6: Parte1.D3_PWM, J1.pin2
  N7: Parte1.D5_PWM, J2.pulse
  5V: Parte1.5V, S1.Pin_3, S1.Pin_4, S2.Pin_3, S2.Pin_4, S3.Pin_3, S3.Pin_4, S5.Pin_3, S5.Pin_4, J2.vcc
  GND: Parte1.GND, R1.Pin_1, R2.Pin_1, R3.Pin_1, R4.Pin_1, R5.Pin_1, J1.pin1, J2.gnd
  N8: S4.Pin_1, S4.Pin_2
  N9: S4.Pin_3, S4.Pin_4
