# Fritzing sketch proyectoshieldl293dne (saved by Fritzing 0.7.12b)
breadboards: 1

parts:
  Arduino1 = Arduino
  J1 = Screw terminal - 2 pins [package=THT]
  J2 = Screw terminal - 2 pins [package=THT]
  U1 = 74HC595 [package="DIP16 [THT]"]
  J3 = Screw terminal - 2 pins [package=THT]
  J4 = Screw terminal - 2 pins [package=THT]

nets:
  N1: Arduino1.GND, J1.pin1, J2.pin1, U1.Q4, U1.Q5, U1.ST_CP, U1.OE
  N2: Arduino1.D11, U1.Q7
  N3: Arduino1.D10, U1.Q2
  N4: Arduino1.D9, U1.Q0
  N5: Arduino1.D6, U1.MR
  VIN: Arduino1.VIN, J1.pin2, U1.Q1, U1.Q7', U1.VCC
  N6: J2.pin2, U1.GND
  N7: U1.Q3, J3.pin1
  N8: U1.Q6, J3.pin2
  N9: U1.SH_CP, J4.pin2
  N10: U1.DS, J4.pin1
