# Fritzing sketch montajeBasico (saved by Fritzing 0.7.12b)
breadboards: 1

parts:
  Arduino1 = Arduino
  LED1 = RGB LED (com. anode, rbg) [package="5 mm [THT]"]
  J1 = Piezo Speaker

nets:
  N1: Arduino1.D12, LED1.green_cathode
  N2: Arduino1.D11, LED1.blue_cathode
  N3: Arduino1.D10, LED1.red_cathode
  N4: Arduino1.D9, J1.pin2
  N5: Arduino1.GND, LED1.common_anode, J1.pin1
