# Fritzing sketch EsquemaConexiones (saved by Fritzing 0.9.2b)
breadboards: 1

parts:
  R1 = Rotary Potentiometer (Small) [maximum_resistance=100kΩ package=THT]
  R2 = Rotary Potentiometer (Small) [maximum_resistance=100kΩ package=THT]
  Parte1 = Arduino Uno (Rev3)

nets:
  N1: R1.leg1, R2.leg1, Parte1.5V
  N2: R1.wiper, Parte1.A0
  N3: R1.leg2, R2.leg2, Parte1.GND
  N4: R2.wiper, Parte1.A1
