# Fritzing sketch esquemaConexiones (saved by Fritzing 0.8.5b)
breadboards: 1

parts:
  LED1 = LED - 5mm [color="Red (633nm)" package="5 mm [THT]"]  # not connected
  R2 = Photocell (LDR) [package=THT]
  LED2 = LED - 5mm [color="Red (633nm)" package="5 mm [THT]"]
  Q1 = NPN-Transistor [package="TO92 [THT]"]
  R3 = Rotary Potentiometer (Small) [maximum_resistance=100kΩ package=THT]
  VCC1 = Battery

nets:
  N1: R2.pin_0, Q1.B, R3.leg2
  N2: R2.pin_1, LED2.cathode, VCC1.-
  N3: LED2.anode, Q1.E
  N4: Q1.C, R3.wiper, VCC1.+
